# Fritzing sketch Robot (saved by Fritzing 0.8.7b)
breadboards: 1

parts:
  Part1 = SRF05 Ultrasonic Rangefinder
  S1 = H-Bridge with L298N
  Part2 = Arduino Uno (Rev3)
  M1 = DC Motor
  M2 = DC Motor
  J1 = Basic Servo  # not connected
  LED1 = LED - 5mm [color="Red (633nm)" package="5 mm [THT]"]
  LED2 = LED - 5mm [color="Red (633nm)" package="5 mm [THT]"]

nets:
  VCC: Part1.VCC, S1.5V, S1.ENA-5V, S1.ENB-5V
  N1: Part1.Trig, Part2.D8
  N2: Part1.Echo, Part2.D9_PWM
  GND: Part1.GND, S1.GND, LED1.cathode, LED2.cathode
  N3: S1.ENA, S1.ENB, Part2.D5_PWM
  N4: S1.IN1, Part2.A3
  N5: S1.IN2, Part2.A2
  N6: S1.IN3, Part2.A1
  N7: S1.IN4, Part2.A0
  N8: S1.M1-01, M1.pin_2
  N9: S1.M1-02, M1.pin_1
  N10: S1.M2-01, M2.pin_1
  N11: S1.M2-02, M2.pin_2

custom parts:
  H-Bridge with L298N: h-bridge
